# Fritzing sketch LED_Clock (saved by Fritzing 0.9.3b)
breadboards: 1

parts:
  (0_0) = Header 3 [part_number=SS:48 package=1x03-1mm-ra]
  (0_1) = Header 3 [part_number=SS:46 package=1x03-1mm-ra]
  (0_2) = Header 3 [part_number=SS:49 package=1x03-1mm-ra]
  (0_3) = Header 3 [part_number=SS:47 package=1x03-1mm-ra]
  (0_4) = Header 3 [part_number=SS:45 package=1x03-1mm-ra]
  (0_5) = Header 3 [part_number=SS:43 package=1x03-1mm-ra]
  (0_6) = Header 3 [part_number=SS:41 package=1x03-1mm-ra]
  (0_7) = Header 3 [part_number=SS:39 package=1x03-1mm-ra]
  Part1 = Arduino Mega 2560 (Rev3)
  (1_0) = Header 3 [part_number=SS:36 package=1x03-1mm-ra]
  (1_6) = Header 3 [part_number=SS:24 package=1x03-1mm-ra]
  (1_5) = Header 3 [part_number=SS;26 package=1x03-1mm-ra]
  (1_2) = Header 3 [part_number=SS:32 package=1x03-1mm-ra]
  (1_7) = Header 3 [part_number=SS:22 package=1x03-1mm-ra]
  (1_4) = Header 3 [part_number=SS:28 package=1x03-1mm-ra]
  (1_1) = Header 3 [part_number=SS:34 package=1x03-1mm-ra]
  (1_3) = Header 3 [part_number=SS:30 package=1x03-1mm-ra]
  (2_5) = Header 3 [part_number=SS:27 package=1x03-1mm-ra]
  (2_2) = Header 3 [part_number=SS:33 package=1x03-1mm-ra]
  (2_6) = Header 3 [part_number=SS:25 package=1x03-1mm-ra]
  (2_0) = Header 3 [part_number=SS:37 package=1x03-1mm-ra]
  (2_1) = Header 3 [part_number=SS:35 package=1x03-1mm-ra]
  (2_7) = Header 3 [part_number=SS:23 package=1x03-1mm-ra]
  (2_3) = Header 3 [part_number=SS:31 package=1x03-1mm-ra]
  (2_4) = Header 3 [part_number=SS:29 package=1x03-1mm-ra]
  U2 = ESP8266 WiFi Module [part_number=ESP8266]
  R1 = Resistor [tolerance=±5% resistance=10k package=THT]
  R2 = Resistor [tolerance=±5% resistance=20k package=THT]
  R3 = PHOTOCELL [package=photocell-kit]
  R4 = Resistor [tolerance=±5% resistance=10k package=THT]
  DS1 = DS18B20 1-Wire Temperature Sensor [part_number=DS18B20]
  R5 = Resistor [tolerance=±5% resistance=4.7k package=THT]

nets:
  N1: (0_0).MOSI, (0_1).MOSI, (0_2).MOSI, (0_3).MOSI, (0_4).MOSI, (0_5).MOSI, (0_6).MOSI, (0_7).MOSI, Part1.D53, (1_0).MOSI, (1_6).MOSI, (1_5).MOSI, (1_2).MOSI, (1_7).MOSI, (1_4).MOSI, (1_1).MOSI, (1_3).MOSI, (2_5).MOSI, (2_2).MOSI, (2_6).MOSI, (2_0).MOSI, (2_1).MOSI, (2_7).MOSI, (2_3).MOSI, (2_4).MOSI
  N2: (0_0).SCK, (0_1).SCK, (0_2).SCK, (0_3).SCK, (0_4).SCK, (0_5).SCK, (0_6).SCK, (0_7).SCK, Part1.D52, (1_0).SCK, (1_6).SCK, (1_5).SCK, (1_2).SCK, (1_7).SCK, (1_4).SCK, (1_1).SCK, (1_3).SCK, (2_5).SCK, (2_2).SCK, (2_6).SCK, (2_0).SCK, (2_1).SCK, (2_7).SCK, (2_3).SCK, (2_4).SCK
  N3: (0_0).SS, Part1.D46
  N4: (0_1).SS, Part1.D48
  N5: (0_2).SS, Part1.D49
  N6: (0_3).SS, Part1.D47
  N7: (0_4).SS, Part1.D45
  N8: (0_5).SS, Part1.D43
  N9: (0_6).SS, Part1.D41
  N10: (0_7).SS, Part1.D39
  N11: Part1.A0, R3.P$2, R4.Pin_0
  N12: Part1.D19/RX1, U2.TXD
  N13: Part1.D18/TX1, R1.Pin_1
  GND: Part1.GND, U2.GND, R2.Pin_0, R3.P$1, DS1.GND
  5V: Part1.VIN, R4.Pin_1, DS1.VDD, R5.Pin_0
  N14: Part1.D22, (1_7).SS
  N15: Part1.D23, (2_7).SS
  N16: Part1.D24, (1_6).SS
  N17: Part1.D25, (2_6).SS
  N18: Part1.D26, (1_5).SS
  N19: Part1.D27, (2_5).SS
  N20: Part1.D28, (1_4).SS
  N21: Part1.D29, (2_4).SS
  N22: Part1.D30, (1_3).SS
  N23: Part1.D31, (2_3).SS
  N24: Part1.D32, (1_2).SS
  N25: Part1.D33, (2_2).SS
  N26: Part1.D34, (1_1).SS
  N27: Part1.D35, (2_1).SS
  N28: Part1.D36, (1_0).SS
  N29: Part1.D37, (2_0).SS
  N30: Part1.D44, DS1.DQ, R5.Pin_1
  N31: U2.RXD, R1.Pin_0, R2.Pin_1
  3.3V: U2.VCC, U2.CH_PD

notes:
  LED Display (8x3)

custom parts:
  Header 3: Header 3 Standard 3-pin 0.1 header. Use with straight break away headers (SKU : PRT-00116), right angle break away headers (PRT-00553), swiss pins (PRT-00743), machine pins (PRT-00117), and female headers (PRT-00115). Molex polarized connector foot print use with SKU : PRT-08232 with associated crimp pins and housings.
  ESP8266 WiFi Module: Generic WiFi Module based on the ESP8266 with onboard PCB antenna and UART communications
