# Fritzing sketch LED Matrix SPI (saved by Fritzing 0.9.2b)
breadboards: 1

parts:
  MAX7219 = MAX7219 [package=dil24]
  788BS = LBT2088AH [part_number=LBT2088AH]
  C3 = Ceramic Capacitor [capacitance=10µF package="100 mil [THT, multilayer]"]
  C4 = Ceramic Capacitor [capacitance=0.1µF package="100 mil [THT, multilayer]"]
  R2 = Resistor [tolerance=±5% resistance=33k package=THT]
  R3 = Resistor [tolerance=±5% resistance=10k package=THT]

nets:
  MOSI: MAX7219.DIN
  N1: MAX7219.DIG0, 788BS.pin_13
  N2: MAX7219.DIG4, 788BS.pin_6
  GND: MAX7219.GND, MAX7219.GND2, C3.0, C4.0, R3.Pin_1
  N3: MAX7219.DIG6, 788BS.pin_15
  N4: MAX7219.DIG2, 788BS.pin_4
  N5: MAX7219.DIG3, 788BS.pin_10
  N6: MAX7219.DIG7, 788BS.pin_16
  N7: MAX7219.DIG5, 788BS.pin_11
  N8: MAX7219.DIG1, 788BS.pin_3
  SS: MAX7219.LOAD, R3.Pin_0
  SCK: MAX7219.CLK
  N9: MAX7219.SEGA, 788BS.pin2
  N10: MAX7219.SEGF, 788BS.pin_14
  N11: MAX7219.SEGB, 788BS.pin_7
  N12: MAX7219.SEGG, 788BS.pin_9
  N13: MAX7219.ISET, R2.Pin_0
  5V: MAX7219.VCC, C3.1, C4.1, R2.Pin_1
  N14: MAX7219.SEGC, 788BS.pin1
  N15: MAX7219.SEGE, 788BS.pin_8
  N16: MAX7219.SEGDP, 788BS.pin_5
  N17: MAX7219.SEGD, 788BS.pin_12
  MISO: MAX7219.DOUT

notes:
  MOSI - 51
  MISO - ??
  SS - ??
  SCK - 52

custom parts:
  MAX7219: 8-digit, 8-segment LED display driver, serial input
